// Logisim project 0001 A - B.circ as structural Verilog: 1 circuit, main circuit sub v2 To use
// B-A
module sub_v2_To_use (
  input  A0,
  input  B0,
  input  A1,
  input  B1,
  input  A2,
  input  B2,
  input  A3,
  input  B3,
  output [7:0] A___B,
  output borrow_flag
);

  wire subtractor_1_bout, subtractor_2_bout, subtractor_3_bout;

  Subtractor #(.width(1)) subtractor_1 (.a(A0), .b(B0), .out(A___B[0]), .bin(1'b0), .bout(subtractor_1_bout));
  Subtractor #(.width(1)) subtractor_2 (
    .a(A1), .b(B1), .out(A___B[1]), .bin(subtractor_1_bout), .bout(subtractor_2_bout));
  Subtractor #(.width(1)) subtractor_3 (
    .a(A2), .b(B2), .out(A___B[2]), .bin(subtractor_2_bout), .bout(subtractor_3_bout));
  Subtractor #(.width(1)) subtractor_4 (.a(A3), .b(B3), .out(A___B[3]), .bin(subtractor_3_bout), .bout(borrow_flag));

  assign A___B[7:4] = 4'b0000;

  // Other names for the same wires on the sheet: X0 = A___B[0]; X1 = A___B[1]; X2 = A___B[2]; X3 = A___B[3]
endmodule
