// Logisim project 0010 B-A.circ as structural Verilog: 1 circuit, main circuit sub v2 To use
// B-A
module sub_v2_To_use (
  input  B0,
  input  A0,
  input  B1,
  input  A1,
  input  B2,
  input  A2,
  input  B3,
  input  A3,
  output [7:0] B_A,
  output borrow_flag
);

  wire subtractor_1_bout, subtractor_2_bout, subtractor_3_bout;

  Subtractor #(.width(1)) subtractor_1 (.a(B0), .b(A0), .out(B_A[0]), .bin(1'b0), .bout(subtractor_1_bout));
  Subtractor #(.width(1)) subtractor_2 (
    .a(B1), .b(A1), .out(B_A[1]), .bin(subtractor_1_bout), .bout(subtractor_2_bout));
  Subtractor #(.width(1)) subtractor_3 (
    .a(B2), .b(A2), .out(B_A[2]), .bin(subtractor_2_bout), .bout(subtractor_3_bout));
  Subtractor #(.width(1)) subtractor_4 (.a(B3), .b(A3), .out(B_A[3]), .bin(subtractor_3_bout), .bout(borrow_flag));

  assign B_A[7:4] = 4'b0000;

  // Other names for the same wires on the sheet: X0 = B_A[0]; X1 = B_A[1]; X2 = B_A[2]; X3 = B_A[3]
endmodule
