// Logisim project 0011 Multiply A&B.circ as structural Verilog: 1 circuit, main circuit 0011 Multiply A&B
module _0011_Multiply_A_B (
  input  A3,
  input  A2,
  input  A1,
  input  A0,
  input  B3,
  input  B2,
  input  B1,
  input  B0,
  output [7:0] Multiply_A_B
);

  wire adder_1_cout, adder_2_cout, adder_2_out, adder_3_cout, adder_3_out, adder_4_cout, adder_4_out,
       adder_5_cout, adder_6_cout, adder_6_out, adder_7_cout, adder_7_out, adder_8_cout, adder_8_out,
       adder_9_cout, adder_10_cout, adder_11_cout, and_2_out, and_3_out, and_4_out, and_5_out, and_6_out,
       and_7_out, and_8_out, and_9_out, and_10_out, and_11_out, and_12_out, and_13_out, and_14_out,
       and_15_out, and_16_out;

  and and_1 (Multiply_A_B[0], A0, B0);
  and and_2 (and_2_out, A1, B0);
  and and_3 (and_3_out, A0, B1);
  and and_4 (and_4_out, A2, B0);
  and and_5 (and_5_out, A1, B1);
  and and_6 (and_6_out, A3, B0);
  and and_7 (and_7_out, A2, B1);
  and and_8 (and_8_out, A3, B1);
  Adder #(.width(1)) adder_1 (.a(and_2_out), .b(and_3_out), .out(Multiply_A_B[1]), .cin(1'b0), .cout(adder_1_cout));
  Adder #(.width(1)) adder_2 (.a(and_4_out), .b(and_5_out), .out(adder_2_out), .cin(adder_1_cout), .cout(adder_2_cout));
  Adder #(.width(1)) adder_3 (.a(and_6_out), .b(and_7_out), .out(adder_3_out), .cin(adder_2_cout), .cout(adder_3_cout));
  Adder #(.width(1)) adder_4 (.a(1'b0), .b(and_8_out), .out(adder_4_out), .cin(adder_3_cout), .cout(adder_4_cout));
  and and_9 (and_9_out, A3, B2);
  and and_10 (and_10_out, A0, B2);
  and and_11 (and_11_out, A1, B2);
  and and_12 (and_12_out, A2, B2);
  and and_13 (and_13_out, A3, B3);
  Adder #(.width(1)) adder_5 (.a(adder_2_out), .b(and_10_out), .out(Multiply_A_B[2]), .cin(1'b0), .cout(adder_5_cout));
  Adder #(.width(1)) adder_6 (
    .a(adder_3_out), .b(and_11_out), .out(adder_6_out), .cin(adder_5_cout), .cout(adder_6_cout));
  Adder #(.width(1)) adder_7 (
    .a(adder_4_out), .b(and_12_out), .out(adder_7_out), .cin(adder_6_cout), .cout(adder_7_cout));
  Adder #(.width(1)) adder_8 (
    .a(adder_4_cout), .b(and_9_out), .out(adder_8_out), .cin(adder_7_cout), .cout(adder_8_cout));
  and and_14 (and_14_out, A0, B3);
  and and_15 (and_15_out, A1, B3);
  and and_16 (and_16_out, A2, B3);
  Adder #(.width(1)) adder_9 (.a(adder_6_out), .b(and_14_out), .out(Multiply_A_B[3]), .cin(1'b0), .cout(adder_9_cout));
  Adder #(.width(1)) adder_10 (
    .a(adder_7_out), .b(and_15_out), .out(Multiply_A_B[4]), .cin(adder_9_cout), .cout(adder_10_cout));
  Adder #(.width(1)) adder_11 (
    .a(adder_8_out), .b(and_16_out), .out(Multiply_A_B[5]), .cin(adder_10_cout), .cout(adder_11_cout));
  Adder #(.width(1)) adder_12 (
    .a(adder_8_cout), .b(and_13_out), .out(Multiply_A_B[6]), .cin(adder_11_cout), .cout(Multiply_A_B[7]));

  // Other names for the same wires on the sheet: X0 = Multiply_A_B[0]; X1 = Multiply_A_B[1]; X2 = Multiply_A_B[2];
  //   X3 = Multiply_A_B[3]; X4 = Multiply_A_B[4]; X5 = Multiply_A_B[5]; X6 = Multiply_A_B[6]; X7 = Multiply_A_B[7]
endmodule
