// Logisim project 0100 Bitwise AND.circ as structural Verilog: 1 circuit, main circuit main
module main (
  input  B3,
  input  B2,
  input  B1,
  input  B0,
  input  A3,
  input  A2,
  input  A1,
  input  A0,
  output [7:0] AND_Bitwise
);

  and and_1 (AND_Bitwise[3], A3, B3);
  and and_2 (AND_Bitwise[2], A2, B2);
  and and_3 (AND_Bitwise[1], A1, B1);
  and and_4 (AND_Bitwise[0], A0, B0);

  assign AND_Bitwise[7:4] = 4'b0000;

  // Other names for the same wires on the sheet: X0 = AND_Bitwise[0]; X1 = AND_Bitwise[1]; X2 = AND_Bitwise[2];
  //   X3 = AND_Bitwise[3]
endmodule
