// Logisim project 0101 Bitwise OR.circ as structural Verilog: 1 circuit, main circuit main
module main (
  input  B3,
  input  B2,
  input  B1,
  input  B0,
  input  A3,
  input  A2,
  input  A1,
  input  A0,
  output [7:0] OR_Bitwise
);

  buf or_1 (OR_Bitwise[3], A3);  // OR_Gate
  or or_2 (OR_Bitwise[2], A2, B2);
  or or_3 (OR_Bitwise[1], A1, B1);
  or or_4 (OR_Bitwise[0], A0, B0);

  assign OR_Bitwise[7:4] = 4'b0000;

  // Other names for the same wires on the sheet: X0 = OR_Bitwise[0]; X1 = OR_Bitwise[1]; X2 = OR_Bitwise[2];
  //   X3 = OR_Bitwise[3]
endmodule
