// Logisim project 0110 4 input XOR.circ as structural Verilog: 2 circuits, main circuit main
module main (
  input  a0,
  input  b0,
  input  a1,
  input  b1,
  input  a2,
  input  b2,
  input  a3,
  input  b3,
  output [7:0] X
);

  _1_bit_XOR u_1_bit_xor_1 (.a(a0), .b(b0), .a_b(X[0]));
  _1_bit_XOR u_1_bit_xor_2 (.a(a1), .b(b1), .a_b(X[1]));
  _1_bit_XOR u_1_bit_xor_3 (.a(a2), .b(b2), .a_b(X[2]));
  _1_bit_XOR u_1_bit_xor_4 (.a(a3), .b(b3), .a_b(X[3]));

  assign X[7:4] = 4'b0000;
endmodule

module _1_bit_XOR (
  input  a,
  input  b,
  output a_b
);

  wire and_1_out, and_2_out, not_1_out, not_2_out;

  not not_1 (not_1_out, a);
  and and_1 (and_1_out, a, not_2_out);
  not not_2 (not_2_out, b);
  and and_2 (and_2_out, b, not_1_out);
  or or_1 (a_b, and_1_out, and_2_out);
endmodule
