// Logisim project 0111 Bit-wise NAND (A NAND B).circ as structural Verilog: 1 circuit, main circuit 0111 Bit-wise NAND (A NAND B)
module _0111_Bit_wise_NAND__A_NAND_B (
  input  B3,
  input  B2,
  input  B1,
  input  B0,
  input  A3,
  input  A2,
  input  A1,
  input  A0,
  output [7:0] Bit_wise_NAND
);

  wire not_1_out, not_2_out, not_3_out, not_4_out, not_5_out, not_6_out, not_7_out, not_8_out;

  not not_1 (not_1_out, B3);
  or or_1 (Bit_wise_NAND[3], not_1_out, not_2_out);
  not not_2 (not_2_out, A3);
  not not_3 (not_3_out, B2);
  or or_2 (Bit_wise_NAND[2], not_3_out, not_4_out);
  not not_4 (not_4_out, A2);
  not not_5 (not_5_out, B1);
  or or_3 (Bit_wise_NAND[1], not_5_out, not_6_out);
  not not_6 (not_6_out, A1);
  not not_7 (not_7_out, A0);
  or or_4 (Bit_wise_NAND[0], not_7_out, not_8_out);
  not not_8 (not_8_out, B0);

  assign Bit_wise_NAND[7:4] = 4'b0000;
endmodule
