// Logisim project 1000 2's .circ as structural Verilog: 3 circuits, main circuit main
// 2's comp
module main (
  input  A3,
  input  A2,
  input  A1,
  input  A0,
  output [7:0] A_prime
);

  wire n1_s_1_x0, n1_s_1_x1, n1_s_1_x2, n1_s_1_x3;

  _1_s u_1_s_1 (
    .A3(A3), .A2(A2), .A1(A1), .A0(A0), .X7(A_prime[7]), .X6(A_prime[6]), .X5(A_prime[5]), .X4(A_prime[4]),
    .X3(n1_s_1_x3), .X2(n1_s_1_x2), .X1(n1_s_1_x1), .X0(n1_s_1_x0));
  add_one add_one_1 (
    .A0(n1_s_1_x0), .A1(n1_s_1_x1), .A2(n1_s_1_x2), .A3(n1_s_1_x3), .X0(A_prime[0]), .X1(A_prime[1]),
    .X2(A_prime[2]), .X3(A_prime[3]));
endmodule

module _1_s (
  input  A3,
  input  A2,
  input  A1,
  input  A0,
  output X7,
  output X6,
  output X5,
  output X4,
  output X3,
  output X2,
  output X1,
  output X0
);

  not not_1 (X3, A3);
  not not_2 (X2, A2);
  not not_3 (X1, A1);
  not not_4 (X0, A0);

  assign X4 = 1'b0;
  assign X5 = 1'b0;
  assign X6 = 1'b0;
  assign X7 = 1'b0;
endmodule

// Add one
module add_one (
  input  A0,
  input  A1,
  input  A2,
  input  A3,
  output X0,
  output X1,
  output X3,
  output X2
);

  wire adder_1_cout, adder_2_cout, adder_3_cout;

  Adder #(.width(1)) adder_1 (.a(A0), .b(1'b0), .out(X0), .cin(1'b1), .cout(adder_1_cout));
  Adder #(.width(1)) adder_2 (.a(A1), .b(1'b0), .out(X1), .cin(adder_1_cout), .cout(adder_2_cout));
  Adder #(.width(1)) adder_3 (.a(A2), .b(1'b0), .out(X2), .cin(adder_2_cout), .cout(adder_3_cout));
  Adder #(.width(1)) adder_4 (.a(A3), .b(1'b0), .out(X3), .cin(adder_3_cout));  // open: cout
endmodule
