// Logisim project 1001 1's Complement A.circ as structural Verilog: 1 circuit, main circuit 1's complement
module _1_s_complement (
  input  A3,
  input  A2,
  input  A1,
  input  A0,
  output [7:0] A_prime
);

  not not_1 (A_prime[3], A3);
  not not_2 (A_prime[2], A2);
  not not_3 (A_prime[1], A1);
  not not_4 (A_prime[0], A0);

  assign A_prime[7:4] = 4'b0000;
endmodule
