// Logisim project 1010 Shift A left logical.circ as structural Verilog: 1 circuit, main circuit 1010 Shift A left logical
module _1010_Shift_A_left_logical (
  input  A3,
  input  A2,
  input  A1,
  input  A0,
  output [7:0] Shift_A_left_logical
);


  assign Shift_A_left_logical = {4'b0000, A2, A1, A0, 1'b0};
endmodule
