// Logisim project 1011 Right shift logical.circ as structural Verilog: 1 circuit, main circuit main
module main (
  input  a3,
  input  a2,
  input  a1,
  input  a0,
  output [7:0] X
);


  assign X = {{5{1'b0}}, a3, a2, a1};

  // Notes on the sheet:
  //   right shift logical ---->
endmodule
