// Logisim project 1100 Arithmetic Left Shift .circ as structural Verilog: 1 circuit, main circuit main
module main (
  input  A3,
  input  A2,
  input  A1,
  input  A0,
  output X7,
  output X6,
  output X5,
  output X4,
  output X3,
  output X2,
  output X1,
  output X0
);


  assign X0 = 1'b0;
  assign X1 = A0;
  assign X2 = A1;
  assign X3 = A2;
  assign X4 = 1'b0;
  assign X5 = 1'b0;
  assign X6 = 1'b0;
  assign X7 = 1'b0;
endmodule
