// Logisim project 1101 Right arithmetic shift.circ as structural Verilog: 1 circuit, main circuit main
module main (
  input  a0,
  input  a3,
  input  a2,
  input  a1,
  output [7:0] out_5
);


  assign out_5 = {4'b0000, {2{a3}}, a2, a1};

  // Notes on the sheet:
  //   right shift ---->
endmodule
