// Logisim project 1110 Shift A left circular.circ as structural Verilog: 1 circuit, main circuit 1110 Shift A left circular
module _1110_Shift_A_left_circular (
  input  A3,
  input  A2,
  input  A1,
  input  A0,
  output [7:0] Shift_A_left_circular
);


  assign Shift_A_left_circular = {4'b0000, A2, A1, A0, A3};
endmodule
