// Logisim project 1111 Right Circular.circ as structural Verilog: 1 circuit, main circuit right circular
// RSC
module right_circular (
  input  A3,
  input  A2,
  input  A1,
  input  A0,
  output [7:0] A_prime
);


  assign A_prime = {4'b0000, A0, A3, A2, A1};
endmodule
