// Logisim project 7 segment.circ as structural Verilog: 1 circuit, main circuit main
// 7 seg
module main (
  input  X3,
  input  X2,
  input  X1,
  input  X0,
  output a,
  output b,
  output c,
  output d,
  output e,
  output f,
  output g
);

  wire and_1_out, and_2_out, and_3_out, and_4_out, and_5_out, and_6_out, and_7_out, not_1_out, not_2_out,
       not_3_out, not_4_out, not_6_out, not_7_out, or_1_out, xor_1_out, xor_2_out, xor_3_out, xor_4_out;

  not not_1 (not_1_out, X2);
  not not_2 (not_2_out, X0);
  xor xor_1 (xor_1_out, X2, X0);
  xor xor_2 (xor_2_out, X1, X0);
  and and_1 (and_1_out, X2, X0);
  not not_3 (not_3_out, xor_1_out);
  and and_2 (and_2_out, not_1_out, not_2_out, X1);
  and and_3 (and_3_out, not_1_out, not_2_out);
  not not_4 (not_4_out, and_1_out);
  and and_4 (and_4_out, not_1_out, X0);
  and and_5 (and_5_out, X2, not_2_out);
  not not_5 (c, and_2_out);
  and and_6 (and_6_out, not_2_out, X1);
  or or_1 (or_1_out, and_4_out, X1);
  xor xor_3 (xor_3_out, X2, X1);
  or or_2 (a, X3, X1, not_3_out);
  and and_7 (and_7_out, X2, xor_2_out);
  not not_6 (not_6_out, xor_4_out);
  xor xor_4 (xor_4_out, not_4_out, X1);
  not not_7 (not_7_out, or_1_out);
  not not_8 (b, and_7_out);
  or or_3 (e, and_3_out, and_6_out);
  or or_4 (f, not_7_out, and_5_out, X3);
  or or_5 (g, and_6_out, xor_3_out, X3);
  or or_6 (d, and_3_out, not_6_out, X3);
  _7_Segment_Display u_7_segment_display_1 (.g(g), .f(f), .a(a), .b(b), .e(e), .d(d), .c(c));  // open: dp

  // Notes on the sheet:
  //   B'
  //   D'
  //   B'D'
  //   B'.D
  //   CD'
endmodule
