// Logisim project Zero_Flag.circ as structural Verilog: 1 circuit, main circuit main
module main (
  input  X7,
  input  X6,
  input  X5,
  input  X4,
  input  X3,
  input  X2,
  input  X1,
  input  X0,
  output Z
);

  nor nor_1 (Z, X7, X6, X5, X4, X3, X2, X1, X0);
endmodule
