// Logisim project ~ ALU ~.circ as structural Verilog
// AND
module ALU (
  input  [7:0] i,
  input  [3:0] operation,
  output [7:0] out_3
);

  wire and_1_out, arithmetic_operations_1_a_b_carry, arithmetic_operations_1_a_b_carry_2,
       arithmetic_operations_1_b_a_carry, main_1_a, main_1_b, main_1_c, main_1_d, main_1_e, main_1_f,
       main_1_g, main_2_a, main_2_b, main_2_c, main_2_d, main_2_e, main_2_f, main_2_g, multiplexer_1_out,
       nor_1_out, zero_flag_1_out_2;
  wire [7:0] arithmetic_operations_1_out_5, arithmetic_operations_1_out_6, arithmetic_operations_1_out_7,
       arithmetic_operations_1_out_8, bitwise_operations_1__1000, bitwise_operations_1__1001,
       bitwise_operations_1__1010, bitwise_operations_1__1011, bitwise_operations_1__1100,
       bitwise_operations_1__1101, bitwise_operations_1__1110, bitwise_operations_1__1111,
       logic_operators_1_out_2, logic_operators_1_out_3, logic_operators_1_out_4, logic_operators_1_out_5;

  Multiplexer #(.select(2), .enable("false")) multiplexer_1 (
    .in0(arithmetic_operations_1_a_b_carry_2), .in1(arithmetic_operations_1_a_b_carry),
    .in2(arithmetic_operations_1_b_a_carry), .in3(1'b0), .out(multiplexer_1_out), .sel(operation[1:0]));
  nor nor_1 (nor_1_out, operation[2], operation[3]);
  and and_1 (and_1_out, multiplexer_1_out, nor_1_out);
  LED Carry (.in(and_1_out));
  Bitwise_operations bitwise_operations_1 (
    ._1000(bitwise_operations_1__1000), ._1001(bitwise_operations_1__1001), .\input (i),
    ._1100(bitwise_operations_1__1100), ._1010(bitwise_operations_1__1010),
    ._1011(bitwise_operations_1__1011), ._1101(bitwise_operations_1__1101),
    ._1110(bitwise_operations_1__1110), ._1111(bitwise_operations_1__1111));
  Arithmetic_operations arithmetic_operations_1 (
    .i(i), .out_7(arithmetic_operations_1_out_7), .out_6(arithmetic_operations_1_out_6),
    .out_5(arithmetic_operations_1_out_5), .out_8(arithmetic_operations_1_out_8),
    .A_B_carry(arithmetic_operations_1_a_b_carry), .B_A_carry(arithmetic_operations_1_b_a_carry),
    .A_B_carry_2(arithmetic_operations_1_a_b_carry_2));
  Logic_operators logic_operators_1 (
    .out_2(logic_operators_1_out_2), .out_3(logic_operators_1_out_3), .out_4(logic_operators_1_out_4),
    .out_5(logic_operators_1_out_5), .in_1(i));
  Multiplexer #(.select(4), .width(8), .enable("false")) multiplexer_2 (
    .in0(arithmetic_operations_1_out_7), .in1(arithmetic_operations_1_out_8),
    .in2(arithmetic_operations_1_out_5), .in3(arithmetic_operations_1_out_6), .in4(logic_operators_1_out_2),
    .in5(logic_operators_1_out_3), .in6(logic_operators_1_out_4), .in7(logic_operators_1_out_5),
    .in8(bitwise_operations_1__1000), .in9(bitwise_operations_1__1001), .in10(bitwise_operations_1__1010),
    .in11(bitwise_operations_1__1011), .in12(bitwise_operations_1__1100), .in13(bitwise_operations_1__1101),
    .in14(bitwise_operations_1__1110), .in15(bitwise_operations_1__1111), .out(out_3), .sel(operation));
  LED _64 (.in(out_3[6]));
  LED _128 (.in(out_3[7]));
  LED _16 (.in(out_3[4]));
  LED _32 (.in(out_3[5]));
  zero_flag zero_flag_1 (.in_1(out_3), .out_2(zero_flag_1_out_2));
  LED _1 (.in(out_3[0]));
  LED _4 (.in(out_3[2]));
  LED _8 (.in(out_3[3]));
  LED _2 (.in(out_3[1]));
  LED zero_flag_2 (.in(zero_flag_1_out_2));
  _7_Segment_Display u_7_segment_display_1 (
    .g(main_1_g), .f(main_1_f), .a(main_1_a), .b(main_1_b), .e(main_1_e), .d(main_1_d), .c(main_1_c));  // open: dp
  _7_segment_main main_1 (
    .X3(i[7]), .X2(i[6]), .X1(i[5]), .X0(i[4]), .a(main_1_a), .b(main_1_b), .c(main_1_c), .d(main_1_d),
    .e(main_1_e), .f(main_1_f), .g(main_1_g));
  _7_Segment_Display u_7_segment_display_2 (
    .g(main_2_g), .f(main_2_f), .a(main_2_a), .b(main_2_b), .e(main_2_e), .d(main_2_d), .c(main_2_c));  // open: dp
  _7_segment_main main_2 (
    .X3(i[3]), .X2(i[2]), .X1(i[1]), .X0(i[0]), .a(main_2_a), .b(main_2_b), .c(main_2_c), .d(main_2_d),
    .e(main_2_e), .f(main_2_f), .g(main_2_g));

  // Notes on the sheet:
  //   B
  //   A
endmodule

module full_adder (
);

  // _0000_4_input_full_adder_main main_1: pin names not known
endmodule

module A_B (
);

  // sub_v2_To_use sub_v2_to_use_1: pin names not known
endmodule

module B_A (
);

  // sub_v2_To_use sub_v2_to_use_1: pin names not known
endmodule

module A___B (
);

  // _0011_Multiply_A_B 0011_multiply_a_b_1: pin names not known
endmodule

module circuit (
);

  // _0100_Bitwise_AND_main main_1: pin names not known
endmodule

module OR (
);

  // _0101_Bitwise_OR_main main_1: pin names not known
endmodule

module circuit_2 (
);

  // _0110_4_input_XOR_main main_1: pin names not known
endmodule

module NAND (
);

  // _0111_Bit_wise_NAND__A_NAND_B 0111_bit_wise_nand_a_nand_b_1: pin names not known
endmodule

module _2_s_complement (
);

  // add_one add_one_1: pin names not known
  // _1000_2_s__main main_1: pin names not known
endmodule

module _1_s_new (
  input  A3,
  input  A2,
  input  A1,
  input  A0,
  output [7:0] X4
);

  not not_1 (X4[3], A3);
  not not_2 (X4[2], A2);
  not not_3 (X4[1], A1);
  not not_4 (X4[0], A0);

  assign X4[7:4] = 4'b0000;
endmodule

module LSL (
);

  wire [3:0] i;
  wire [7:0] LSL;

  // _1010_Shift_A_left_logical 1010_shift_a_left_logical_1: pin names not known
  _1010_Shift_A_left_logical u_1010_shift_a_left_logical_2 (
    .A3(i[3]), .A2(i[2]), .A1(i[1]), .A0(i[0]), .Shift_A_left_logical(LSL));
endmodule

module RSL (
);

  // _1011_Right_shift_logical_main main_1: pin names not known
endmodule

module LSA (
  input  A3,
  input  A2,
  input  A1,
  input  A0,
  output [7:0] out_5
);

  _1100_Arithmetic_Left_Shift__main main_1 (
    .A3(A3), .A2(A2), .A1(A1), .A0(A0), .X7(out_5[7]), .X6(out_5[6]), .X5(out_5[5]), .X4(out_5[4]),
    .X3(out_5[3]), .X2(out_5[2]), .X1(out_5[1]), .X0(out_5[0]));
endmodule

module Arithmetic_operations (
  input  [7:0] i,
  output B_A_carry,
  output A_B_carry,
  output A_B_carry_2,
  output [7:0] out_5,
  output [7:0] out_6,
  output [7:0] out_7,
  output [7:0] out_8
);

  _0000_4_input_full_adder_main main_1 (
    .X(out_7), .a0(i[0]), .b0(i[4]), .a1(i[1]), .b1(i[5]), .a2(i[2]), .b2(i[6]), .a3(i[3]), .b3(i[7]),
    .Carry(A_B_carry_2));
  sub_v2_To_use B_A (
    .B0(i[4]), .A0(i[0]), .B1(i[5]), .A1(i[1]), .B2(i[6]), .A2(i[2]), .B3(i[7]), .A3(i[3]),
    .borrow_flag(B_A_carry), .B_A(out_5));
  sub_v2_To_use sub_v2_to_use_1 (
    .A0(i[0]), .B0(i[4]), .A1(i[1]), .B1(i[5]), .A2(i[2]), .B2(i[6]), .A3(i[3]), .B3(i[7]),
    .borrow_flag(A_B_carry), .A___B(out_8));
  _0011_Multiply_A_B u_0011_multiply_a_b_1 (
    .A0(i[0]), .A1(i[1]), .A2(i[2]), .A3(i[3]), .B2(i[6]), .B0(i[4]), .B3(i[7]), .B1(i[5]),
    .Multiply_A_B(out_6));

  // Other names for the same wires on the sheet: _0011[7:0] = out_6

  // Notes on the sheet:
  //   b3 b2 b1 b0 a3 a2 a1 a0
endmodule

module Logic_operators (
  input  [7:0] in_1,
  output [7:0] out_2,
  output [7:0] out_3,
  output [7:0] out_4,
  output [7:0] out_5
);

  _0100_Bitwise_AND_main main_1 (
    .B3(in_1[7]), .B2(in_1[6]), .B1(in_1[5]), .B0(in_1[4]), .A3(in_1[3]), .A2(in_1[2]), .A1(in_1[1]),
    .A0(in_1[0]), .AND_Bitwise(out_2));
  _0101_Bitwise_OR_main main_2 (
    .B3(in_1[7]), .B2(in_1[6]), .B1(in_1[5]), .B0(in_1[4]), .A3(in_1[3]), .A2(in_1[2]), .A1(in_1[1]),
    .A0(in_1[0]), .OR_Bitwise(out_3));
  _0110_4_input_XOR_main main_3 (
    .a0(in_1[7]), .b0(in_1[3]), .a1(in_1[6]), .b1(in_1[2]), .a2(in_1[5]), .b2(in_1[1]), .a3(in_1[4]),
    .b3(in_1[0]), .X(out_4));
  _0111_Bit_wise_NAND__A_NAND_B u_0111_bit_wise_nand_a_nand_b_1 (
    .B3(in_1[0]), .B2(in_1[1]), .B1(in_1[2]), .B0(in_1[3]), .A3(in_1[4]), .A2(in_1[5]), .A1(in_1[6]),
    .A0(in_1[7]), .Bit_wise_NAND(out_5));

  // Other names for the same wires on the sheet: N[7:0] = out_5; OR_0101[7:0] = out_3; tunnel[7:0] = out_4

  // Notes on the sheet:
  //   b3 b2 b1 b0 a3 a2 a1 a0
endmodule

module Bitwise_operations (
  input  [7:0] \input ,
  output [7:0] _1011,
  output [7:0] _1100,
  output [7:0] _1010,
  output [7:0] _1000,
  output [7:0] _1001,
  output [7:0] _1111,
  output [7:0] _1101,
  output [7:0] _1110
);

  _1000_2_s__main main_1 (.A3(\input [3]), .A2(\input [2]), .A1(\input [1]), .A0(\input [0]), .A_prime(_1000));
  _1_s_new u_1_s_new_1 (.A3(\input [3]), .A2(\input [2]), .A1(\input [1]), .A0(\input [0]), .X4(_1001));
  LSA lsa_1 (.A3(\input [3]), .A2(\input [2]), .A1(\input [1]), .A0(\input [0]), .out_5(_1010));
  _1101_Right_arithmetic_shift_main main_2 (
    .a3(\input [3]), .a2(\input [2]), .a1(\input [1]), .a0(\input [0]), .out_5(_1101));
  _1110_Shift_A_left_circular u_1110_shift_a_left_circular_1 (
    .A3(\input [3]), .A2(\input [2]), .A1(\input [1]), .A0(\input [0]), .Shift_A_left_circular(_1110));
  _1011_Right_shift_logical_main main_3 (.a3(\input [3]), .a2(\input [2]), .a1(\input [1]), .a0(\input [0]), .X(_1011));
  right_circular right_circular_1 (.A3(\input [3]), .A2(\input [2]), .A1(\input [1]), .A0(\input [0]), .A_prime(_1111));

  assign _1100 = _1010;

  // Other names for the same wires on the sheet: _1_s[7:0] = _1001; _2_s[7:0] = _1000; i[7:0] = \input ;
  //   LSL_LSA[7:0] = _1010; RSL[7:0] = _1011

  // Notes on the sheet:
  //   b3 b2 b1 b0 a3 a2 a1 a0
endmodule

module zero_flag (
  input  [7:0] in_1,
  output out_2
);

  Zero_Flag_main main_1 (
    .X7(in_1[0]), .X6(in_1[1]), .X5(in_1[2]), .X4(in_1[3]), .X3(in_1[4]), .X2(in_1[5]), .X1(in_1[6]),
    .X0(in_1[7]), .Z(out_2));
endmodule
